// Logisim project cpu_implementation_project.circ as structural Verilog
module register_file (
  input  [31:0] in_1,
  input  in_2,
  input  [2:0] in_3,
  input  [2:0] in_4,
  input  [2:0] in_5,
  input  [2:0] in_6,
  output [31:0] out_7,
  output [31:0] out_8,
  output [31:0] out_9
);

  wire comparator_1_eq, decoder_1_out0, decoder_1_out1, decoder_1_out2, decoder_1_out3, decoder_1_out4,
       decoder_1_out5, decoder_1_out6, decoder_1_out7;
  wire [31:0] adder_1_out, and_1_out, or_1_out, R0_q, R1_q, R2_q, R3_q, R4_q, R5_q, R6_q, R7_q, xnor_1_out;

  Decoder #(.select(3)) decoder_1 (
    .out0(decoder_1_out0), .out1(decoder_1_out1), .out2(decoder_1_out2), .out3(decoder_1_out3),
    .out4(decoder_1_out4), .out5(decoder_1_out5), .out6(decoder_1_out6), .out7(decoder_1_out7), .sel(in_4),
    .en(in_2));
  Register #(.width(32)) R0 (.D(in_1), .en(decoder_1_out0), .Q(R0_q));  // open: clk, clr
  Register #(.width(32)) R1 (.D(in_1), .en(decoder_1_out1), .Q(R1_q));  // open: clk, clr
  Register #(.width(32)) R2 (.D(in_1), .en(decoder_1_out2), .Q(R2_q));  // open: clk, clr
  Register #(.width(32)) R3 (.D(in_1), .en(decoder_1_out3), .Q(R3_q));  // open: clk, clr
  Register #(.width(32)) R4 (.D(in_1), .en(decoder_1_out4), .Q(R4_q));  // open: clk, clr
  Register #(.width(32)) R5 (.D(in_1), .en(decoder_1_out5), .Q(R5_q));  // open: clk, clr
  Register #(.width(32)) R6 (.D(in_1), .en(decoder_1_out6), .Q(R6_q));  // open: clk, clr
  Register #(.width(32)) R7 (.D(in_1), .en(decoder_1_out7), .Q(R7_q));  // open: clk, clr
  Adder #(.width(32)) adder_1 (.a(out_7), .b(out_8), .out(adder_1_out));  // open: cin, cout
  assign or_1_out = out_7 | out_8;  // OR_Gate or_1, 32 bits wide
  assign and_1_out = out_7 & out_8;  // AND_Gate and_1, 32 bits wide
  assign xnor_1_out = ~(out_7 ^ out_8);  // XNOR_Gate xnor_1, 32 bits wide
  Multiplexer #(.select(3), .width(32)) multiplexer_1 (
    .in1(adder_1_out), .in2(or_1_out), .in3(and_1_out), .in4(xnor_1_out), .out(out_9), .sel(in_6));  // open: in0, in5, in6, in7
  Comparator #(.width(32)) comparator_1 (.a(out_7), .b(out_8), .eq(comparator_1_eq));  // open: gt, lt
  LED led_1 (.in(comparator_1_eq));
  Multiplexer #(.select(3), .width(32)) multiplexer_2 (
    .in0(R0_q), .in1(R1_q), .in2(R2_q), .in3(R3_q), .in4(R4_q), .in5(R5_q), .in6(R6_q), .in7(R7_q),
    .out(out_7), .sel(in_3));
  Multiplexer #(.select(3), .width(32)) multiplexer_3 (
    .in0(R0_q), .in1(R1_q), .in2(R2_q), .in3(R3_q), .in4(R4_q), .in5(R5_q), .in6(R6_q), .in7(R7_q),
    .out(out_8), .sel(in_5));

  // Notes on the sheet:
  //   ADDER
  //   OR
  //   AND
  //   EQUALS
  //   OUTPUT
endmodule

module cpu (
  input  [31:0] in_1,
  input  in_2,
  input  [2:0] in_3,
  input  [2:0] in_4,
  input  [2:0] in_5,
  input  [2:0] in_6,
  output [31:0] out_7,
  output [31:0] out_8,
  output [31:0] out_9
);

  wire comparator_1_eq, decoder_1_out0, decoder_1_out1, decoder_1_out2, decoder_1_out3, decoder_1_out4,
       decoder_1_out5, decoder_1_out6, decoder_1_out7;
  wire [31:0] adder_1_out, and_1_out, or_1_out, R1_q, R2_q, R3_q, R4_q, R5_q, R6_q, R7_q, undriven,
       xnor_1_out;

  Decoder #(.select(3)) decoder_1 (
    .out0(decoder_1_out0), .out1(decoder_1_out1), .out2(decoder_1_out2), .out3(decoder_1_out3),
    .out4(decoder_1_out4), .out5(decoder_1_out5), .out6(decoder_1_out6), .out7(decoder_1_out7), .sel(in_4),
    .en(in_2));
  Register #(.width(32)) R1 (.D(in_1), .en(decoder_1_out1), .Q(R1_q));  // open: clk, clr
  Register #(.width(32)) R2 (.D(in_1), .en(decoder_1_out2), .Q(R2_q));  // open: clk, clr
  Register #(.width(32)) R3 (.D(in_1), .en(decoder_1_out3), .Q(R3_q));  // open: clk, clr
  Register #(.width(32)) R4 (.D(in_1), .en(decoder_1_out4), .Q(R4_q));  // open: clk, clr
  Register #(.width(32)) R5 (.D(in_1), .en(decoder_1_out5), .Q(R5_q));  // open: clk, clr
  Register #(.width(32)) R6 (.D(in_1), .en(decoder_1_out6), .Q(R6_q));  // open: clk, clr
  Register #(.width(32)) R7 (.D(in_1), .en(decoder_1_out7), .Q(R7_q));  // open: clk, clr
  Adder #(.width(32)) adder_1 (.a(out_7), .b(out_8), .out(adder_1_out));  // open: cin, cout
  assign or_1_out = out_7 | out_8;  // OR_Gate or_1, 32 bits wide
  assign and_1_out = out_7 & out_8;  // AND_Gate and_1, 32 bits wide
  assign xnor_1_out = ~(out_7 ^ out_8);  // XNOR_Gate xnor_1, 32 bits wide
  Multiplexer #(.select(3), .width(32)) multiplexer_1 (
    .in1(adder_1_out), .in2(or_1_out), .in3(and_1_out), .in4(xnor_1_out), .out(out_9), .sel(in_6));  // open: in0, in5, in6, in7
  Comparator #(.width(32)) comparator_1 (.a(out_7), .b(out_8), .eq(comparator_1_eq));  // open: gt, lt
  LED led_1 (.in(comparator_1_eq));
  Multiplexer #(.select(3), .width(32)) multiplexer_2 (
    .in0(undriven), .in1(R1_q), .in2(R2_q), .in3(R3_q), .in4(R4_q), .in5(R5_q), .in6(R6_q), .in7(R7_q),
    .out(out_7), .sel(in_3));
  Multiplexer #(.select(3), .width(32)) multiplexer_3 (
    .in0(undriven), .in1(R1_q), .in2(R2_q), .in3(R3_q), .in4(R4_q), .in5(R5_q), .in6(R6_q), .in7(R7_q),
    .out(out_8), .sel(in_5));

  // Notes on the sheet:
  //   ADDER
  //   OR
  //   AND
  //   EQUALS
  //   OUTPUT
endmodule
